# Fritzing sketch connection_diagram (saved by Fritzing 0.9.3b)
breadboards: 1

parts:
  Mod1 = Raspberry Pi Pico
  U1 = ESP8266 WiFi Module [part_number=ESP8266]
  LED1 = smd LED [color="Red (633nm)" package="0805 [SMD]"]
  LED2 = smd LED [color="Red (633nm)" package="0805 [SMD]"]
  R1 = Resistor [tolerance=±5% resistance=220 package="0805 [SMD]"]
  R2 = Resistor [tolerance=±5% resistance=220 package="0805 [SMD]"]
  U2 = POT [package=pot_mammoth]
  U3 = POT [package=pot_mammoth]
  R3 = Resistor [tolerance=±5% resistance=220 package="0805 [SMD]"]

nets:
  N1: Mod1.pin_3, Mod1.pin_8, Mod1.pin_13, Mod1.pin_18, Mod1.pin_23, Mod1.pin_28, Mod1.pin_33, Mod1.pin_38, U1.GND, LED1.cathode, LED2.cathode, U2.E, U3.E
  N2: Mod1.pin_19, R1.Pin_1
  N3: Mod1.pin_20, R2.Pin_1
  N4: Mod1.pin_21, U1.RXD
  N5: Mod1.pin_22, U1.TXD
  N6: Mod1.pin_31, U3.A
  N7: Mod1.pin_32, U2.A
  N8: Mod1.pin_36, U1.VCC, U2.S, U3.S, R3.Pin_1
  N9: U1.CH_PD, R3.Pin_0
  N10: LED1.anode, R2.Pin_0
  N11: LED2.anode, R1.Pin_0

custom parts:
  Raspberry Pi Pico: Raspberry Pi Pico. Based around the RP2040 microcontroller the Pico is a low cost microcontroller device bringing Raspberry Pi quality, cost, and easy of use to the microcontroller space. Jan 2021, Split part in to two versions: tht (this one) and SMD. This one will drill holes for a .1 in header in pcb to allow plugging in the module as well as providing pads to solder the module to the top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
  ESP8266 WiFi Module: Generic WiFi Module based on the ESP8266 with onboard PCB antenna and UART communications
