# Fritzing sketch pico-w-telegram (saved by Fritzing 0.9.3b)
breadboards: 1

parts:
  Mod1 = Raspberry Pi Pico W
  Parça1 = LCD1602-I2C
  DHT1 = DHT11 Humitidy and Temperature Sensor
  R1 = Resistor [tolerance=±5% resistance=10k package=THT]

nets:
  GND: Mod1.pin_3, Mod1.pin_8, Mod1.pin_13, Mod1.pin_18, Mod1.pin_23, Mod1.pin_28, Mod1.pin_33, Mod1.pin_38, Mod1.pin_42, Parça1.GND, DHT1.GND
  N1: Mod1.pin_6, Parça1.SDA
  N2: Mod1.pin_7, Parça1.SCL
  N3: Mod1.pin_20, Mod1.pin_36, DHT1.VDD, R1.Pin_1
  N4: Mod1.pin_40, Parça1.VCC
  N5: DHT1.DATA, R1.Pin_0

custom parts:
  Raspberry Pi Pico W: Raspberry Pi Pico W. Based around the RP2040 microcontroller the Pico W is a low cost microcontroller device bringing Raspberry Pi quality, cost, and easy of use to the microcontroller space. The areas marked KEEPOUT in pcb silkscreen should not have traces running through them to avoid shorts on a soldered in module!
  LCD1602-I2C: A standard character display, usually with 2x16 characters. Comes in many colors with LCM1602 IIC attached.
  DHT11 Humitidy and Temperature Sensor: DHT11 Humidity and Temperature Sensor
