# Fritzing sketch schematic (saved by Fritzing 0.9.3b)
breadboards: 1

parts:
  Mod1 = Raspberry Pi Pico
  LED1 = smd LED [color="Red (633nm)" package="1206 [SMD]"]
  R1 = Resistor [tolerance=±5% resistance=220 package="1206 [SMD]"]
  LED2 = smd LED [color="Red (633nm)" package="1206 [SMD]"]
  R2 = Resistor [tolerance=±5% resistance=220 package="1206 [SMD]"]
  U1 = POT [package=pot_alpha_rv16af-20]
  S1 = Pushbutton [package="[SMD]"]
  C1 = Electrolytic Capacitor [capacitance=1μF package="0405 [SMD, electrolytic]"]

nets:
  N1: Mod1.pin_3, Mod1.pin_8, Mod1.pin_13, Mod1.pin_18, Mod1.pin_23, Mod1.pin_28, Mod1.pin_33, Mod1.pin_38, LED1.cathode, LED2.cathode, U1.E, S1.Pin_1, S1.Pin_2, C1.-
  N2: Mod1.pin_4, R1.Pin_1
  N3: Mod1.pin_5, R2.Pin_1
  N4: Mod1.pin_6, S1.Pin_3, S1.Pin_4, C1.+
  N5: Mod1.pin_34, U1.S
  N6: Mod1.pin_36, U1.A
  N7: LED1.anode, R1.Pin_0
  N8: LED2.anode, R2.Pin_0

custom parts:
  Raspberry Pi Pico: Raspberry Pi Pico. Based around the RP2040 microcontroller the Pico is a low cost microcontroller device bringing Raspberry Pi quality, cost, and easy of use to the microcontroller space. Jan 2021, Split part in to two versions: tht (this one) and SMD. This one will drill holes for a .1 in header in pcb to allow plugging in the module as well as providing pads to solder the module to the top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
